# Fritzing sketch Fritzing Sketch (saved by Fritzing 0.9.2b)

parts:
  M2 = Stepper Motor - Bipolar
  J1 = Basic Servo
  Raspberry_Pi1 = Raspberry Pi 2
  S1 = Toggle Switch [package=THT]
  S2 = Toggle Switch [package=THT]
  PWM1 = PCA9685 16x12-bit PWM Breakout
  Pi2 = StepperHat
  M1 = Stepper Motor - Bipolar
  R1 = Resistor [tolerance=±5% resistance=220 package=THT]

nets:
  N1: M2.A, Pi2.connector4
  N2: M2.C, Pi2.connector2
  N3: M2.B, Pi2.connector3
  N4: M2.D, Pi2.connector1
  GND: J1.gnd, Raspberry_Pi1.GPIO3, Raspberry_Pi1.GND, Raspberry_Pi1.GPIO18, S1.L2, PWM1.no_name_yet#601, PWM1.no_name_yet#603, PWM1.no_name_yet#1000
  N5: J1.vcc, PWM1.no_name_yet#100
  N6: J1.pulse, PWM1.no_name_yet#0
  3V3: Raspberry_Pi1.3v3, Raspberry_Pi1.GPIO2, Raspberry_Pi1.3V3, Raspberry_Pi1.5V, PWM1.no_name_yet#604, PWM1.no_name_yet#605
  N7: Raspberry_Pi1.GPIO5, S2.COM
  N8: Raspberry_Pi1.GPIO6, S1.COM
  N9: S1.L1, S2.L1, R1.Pin_1
  N10: Pi2.connector6, M1.D
  N11: Pi2.connector7, M1.C
  N12: Pi2.connector8, M1.B
  N13: Pi2.connector9, M1.A

notes:
  Motor X
  Motor Y
  Pen Up-Down
  <--->
  GPIO
